// Logisim project test.circ as structural Verilog
module main (
  input  in_1,
  input  in_2,
  input  in_3,
  input  in_4,
  input  in_5,
  input  in_6,
  input  in_7,
  input  in_8,
  input  in_9,
  input  in_10,
  output out_11,
  output out_12
);

  not not_1 (out_11, in_1);
  // AND_Gate and_1 has open pins: in0=in_3, in1=in_5, out=open
  // AND_Gate and_2 has open pins: in0=in_6, in1=in_7, out=open
  // AND_Gate and_3 has open pins: in0=in_8, in1=in_10, out=open
  not not_2 (out_12, in_2);
  // AND_Gate and_4 has open pins: in0=in_4, in1=in_9, out=open
endmodule

module test (
  input  c,
  output out_2,
  output out_3
);


  assign out_2 = c;
  assign out_3 = c;
endmodule
